// Logisim project B23EE1100_Lab9_ALU.circ as structural Verilog: 2 circuits, main circuit InvertAND4
module main (
  input  [31:0] INPUT_1,
  input  [31:0] INPUT_2,
  input  [3:0] ALU_Control,
  output Zero,
  output Carry,
  output [31:0] ALU_RESULT,
  output Overflow
);

  wire ADD_out_5, adder_1_cout, and_2_out, and_3_out, and_4_out, and_5_out, and_6_out, and_7_out, not_1_out,
       not_2_out, not_3_out, not_4_out, not_5_out, not_6_out, not_7_out, not_8_out, SUB_out_5,
       subtractor_1_bout;
  wire [0:0] comparator_1_lt;
  wire [31:0] adder_1_out, AND_out, bit_extender_1_out, OR_out, subtractor_1_out;

  assign AND_out = INPUT_1 & INPUT_2;  // AND_Gate AND, 32 bits wide
  assign OR_out = INPUT_1 | INPUT_2;  // OR_Gate OR, 32 bits wide
  Adder #(.width(32)) adder_1 (.a(INPUT_1), .b(INPUT_2), .out(adder_1_out), .cout(adder_1_cout));  // open: cin
  Subtractor #(.width(32)) subtractor_1 (
    .a(INPUT_1), .b(INPUT_2), .out(subtractor_1_out), .bout(subtractor_1_bout));  // open: bin
  Comparator #(.width(32)) comparator_1 (.a(INPUT_1), .b(INPUT_2), .lt(comparator_1_lt[0]));  // open: gt, eq
  not not_1 (not_1_out, INPUT_2[31]);
  not not_2 (not_2_out, INPUT_1[31]);
  Multiplexer #(.select(4), .width(32)) multiplexer_1 (
    .in0(AND_out), .in1(OR_out), .in2(adder_1_out), .in6(subtractor_1_out),
    .in7({{31{1'b0}}, comparator_1_lt[0]}), .out(ALU_RESULT), .sel(ALU_Control), .en(1'b1));  // open: in3, in4, in5, in8, in9, in10, in11, in12, in13, in14, in15
  not not_3 (not_3_out, ALU_RESULT[31]);
  not not_4 (not_4_out, 1'b1);
  not not_5 (not_5_out, ALU_Control[1]);
  not not_6 (not_6_out, ALU_Control[1]);
  not not_7 (not_7_out, ALU_Control[2]);
  assign bit_extender_1_out = {{31{1'b0}}, not_4_out};  // Bit_Extender bit_extender_1
  InvertAND4 ADD (
    .in_1(ALU_Control[0]), .in_2(not_5_out), .in_3(ALU_Control[2]), .in_4(ALU_Control[3]), .out_5(ADD_out_5));
  InvertAND4 SUB (.in_1(ALU_Control[0]), .in_2(not_6_out), .in_3(not_7_out), .in_4(ALU_Control[3]), .out_5(SUB_out_5));
  Comparator #(.width(32)) comparator_2 (.a(ALU_RESULT), .b(bit_extender_1_out), .eq(Zero));  // open: gt, lt
  not not_8 (not_8_out, subtractor_1_bout);
  and and_2 (and_2_out, adder_1_cout, ADD_out_5);
  and and_3 (and_3_out, not_8_out, SUB_out_5);
  and and_4 (and_4_out, ADD_out_5, not_3_out, INPUT_1[31], INPUT_2[31]);
  and and_5 (and_5_out, ADD_out_5, ALU_RESULT[31], not_2_out, not_1_out);
  and and_6 (and_6_out, SUB_out_5, INPUT_1[31], not_3_out, not_1_out);
  and and_7 (and_7_out, SUB_out_5, not_2_out, ALU_RESULT[31], INPUT_2[31]);
  or or_2 (Carry, and_2_out, and_3_out);
  or or_3 (Overflow, and_4_out, and_5_out, and_6_out, and_7_out);
endmodule

module InvertAND4 (
  input  in_1,
  input  in_2,
  input  in_3,
  input  in_4,
  output out_5
);

  wire not_1_out, not_2_out, not_3_out, not_4_out;

  not not_1 (not_1_out, in_2);
  not not_2 (not_2_out, in_3);
  not not_3 (not_3_out, in_1);
  not not_4 (not_4_out, in_4);
  and and_1 (out_5, not_3_out, not_1_out, not_2_out, not_4_out);
endmodule
