// Logisim project B23EE1100_Lab9_ALUControlUnit.circ as structural Verilog: 3 circuits, main circuit main
module main (
  input  [2:0] ALUop,
  input  [5:0] in_2,
  output [3:0] out_3
);

  wire ALUop_ADD_IMM_out_4, ALUop_AND_IMM_out_4, ALUop_OR_IMM_out_4, ALUop_SLT_IMM_out_4,
       ALUop_SUB_IMM_out_4, and_1_out, and_2_out, and_3_out, and_4_out, and_5_out, FUNCT_ADD_out_7,
       FUNCT_AND_out_7, FUNCT_OR_out_7, FUNCT_SLT_out_7, FUNCT_SUB_out_7, not_1_out, not_2_out, not_3_out,
       not_4_out, not_5_out, not_6_out, not_7_out, not_8_out, not_9_out, not_10_out, not_11_out, not_12_out,
       not_13_out, not_14_out, not_15_out, not_16_out, not_17_out, not_18_out, or_1_out, or_2_out, or_3_out,
       or_4_out, or_5_out, R_TYPE_out_4;

  not not_1 (not_1_out, in_2[5]);
  not not_2 (not_2_out, in_2[1]);
  not not_3 (not_3_out, in_2[5]);
  not not_4 (not_4_out, in_2[2]);
  not not_5 (not_5_out, in_2[5]);
  not not_6 (not_6_out, in_2[0]);
  not not_7 (not_7_out, in_2[2]);
  not not_8 (not_8_out, in_2[5]);
  not not_9 (not_9_out, in_2[1]);
  not not_10 (not_10_out, in_2[3]);
  not not_11 (not_11_out, in_2[5]);
  InvertAND3 ALUop_ADD_IMM (.in_1(ALUop[2]), .in_2(ALUop[1]), .out_4(ALUop_ADD_IMM_out_4), .in_3(ALUop[0]));
  InvertAND3 ALUop_SUB_IMM (.in_1(ALUop[2]), .in_2(ALUop[1]), .out_4(ALUop_SUB_IMM_out_4), .in_3(not_12_out));
  not not_12 (not_12_out, ALUop[0]);
  InvertAND3 ALUop_SLT_IMM (.in_1(ALUop[2]), .in_2(not_13_out), .out_4(ALUop_SLT_IMM_out_4), .in_3(ALUop[0]));
  not not_13 (not_13_out, ALUop[1]);
  InvertAND3 ALUop_AND_IMM (.in_1(ALUop[2]), .in_2(not_14_out), .out_4(ALUop_AND_IMM_out_4), .in_3(not_15_out));
  not not_14 (not_14_out, ALUop[1]);
  not not_15 (not_15_out, ALUop[0]);
  InvertAND3 ALUop_OR_IMM (.in_1(not_16_out), .in_2(ALUop[1]), .out_4(ALUop_OR_IMM_out_4), .in_3(ALUop[0]));
  not not_16 (not_16_out, ALUop[2]);
  not not_17 (not_17_out, ALUop[2]);
  InvertAND3 R_TYPE (.in_1(not_17_out), .in_2(ALUop[1]), .out_4(R_TYPE_out_4), .in_3(not_18_out));
  not not_18 (not_18_out, ALUop[0]);
  InvertAND6 FUNCT_ADD (
    .in_1(in_2[0]), .in_2(in_2[1]), .in_3(in_2[2]), .in_4(in_2[3]), .out_7(FUNCT_ADD_out_7), .in_5(in_2[4]),
    .in_6(not_1_out));
  InvertAND6 FUNCT_SUB (
    .in_1(in_2[0]), .in_2(not_2_out), .in_3(in_2[2]), .in_4(in_2[3]), .out_7(FUNCT_SUB_out_7),
    .in_5(in_2[4]), .in_6(not_3_out));
  InvertAND6 FUNCT_AND (
    .in_1(in_2[0]), .in_2(in_2[1]), .in_3(not_4_out), .in_4(in_2[3]), .out_7(FUNCT_AND_out_7),
    .in_5(in_2[4]), .in_6(not_5_out));
  InvertAND6 FUNCT_OR (
    .in_1(not_6_out), .in_2(in_2[1]), .in_3(not_7_out), .in_4(in_2[3]), .out_7(FUNCT_OR_out_7),
    .in_5(in_2[4]), .in_6(not_8_out));
  InvertAND6 FUNCT_SLT (
    .in_1(in_2[0]), .in_2(not_9_out), .in_3(in_2[2]), .in_4(not_10_out), .out_7(FUNCT_SLT_out_7),
    .in_5(in_2[4]), .in_6(not_11_out));
  and and_1 (and_1_out, R_TYPE_out_4, FUNCT_ADD_out_7);
  and and_2 (and_2_out, R_TYPE_out_4, FUNCT_SUB_out_7);
  and and_3 (and_3_out, R_TYPE_out_4, FUNCT_AND_out_7);
  and and_4 (and_4_out, R_TYPE_out_4, FUNCT_OR_out_7);
  and and_5 (and_5_out, R_TYPE_out_4, FUNCT_SLT_out_7);
  or or_1 (or_1_out, ALUop_ADD_IMM_out_4, and_1_out);
  or or_2 (or_2_out, ALUop_SUB_IMM_out_4, and_2_out);
  or or_3 (or_3_out, ALUop_AND_IMM_out_4, and_3_out);
  or or_4 (or_4_out, ALUop_OR_IMM_out_4, and_4_out);
  or or_5 (or_5_out, ALUop_SLT_IMM_out_4, and_5_out);
  or or_6 (out_3[0], or_5_out, or_4_out);
  or or_7 (out_3[1], or_1_out, or_2_out, or_5_out);
  or or_8 (out_3[2], or_2_out, or_5_out);

  assign out_3[3] = 1'b0;

  // Notes on the sheet:
  //   (From Main Control Unit)
  //   ADD
  //   SUB
  //   AND
  //   OR
  //   SLT
  //   ALUControl
endmodule

module InvertAND6 (
  input  in_1,
  input  in_2,
  input  in_3,
  input  in_4,
  input  in_5,
  input  in_6,
  output out_7
);

  wire not_1_out, not_2_out, not_3_out, not_4_out, not_5_out, not_6_out;

  not not_1 (not_1_out, in_3);
  not not_2 (not_2_out, in_4);
  not not_3 (not_3_out, in_1);
  not not_4 (not_4_out, in_2);
  not not_5 (not_5_out, in_5);
  not not_6 (not_6_out, in_6);
  and and_1 (out_7, not_3_out, not_4_out, not_1_out, not_2_out, not_5_out, not_6_out);
endmodule

module InvertAND3 (
  input  in_1,
  input  in_2,
  input  in_3,
  output out_4
);

  wire not_1_out, not_2_out, not_3_out;

  not not_1 (not_1_out, in_1);
  not not_2 (not_2_out, in_2);
  not not_3 (not_3_out, in_3);
  and and_1 (out_4, not_1_out, not_2_out, not_3_out);
endmodule
