// Logisim project B23EE1100_Lab9_CompleteProcessor .circ as structural Verilog: 1 circuit, main circuit main
module main (
  input  [4:0] in_1,
  input  in_2,
  input  in_3,
  input  Reset,
  input  Data_Mem_RESET,
  output [31:0] out_6,
  output [31:0] out_7,
  output [31:0] out_8,
  output [31:0] out_9,
  output [31:0] out_10,
  output [23:0] out_11
);

  wire and_1_out, Clock_out, main_3_alusrc, main_3_branch, main_3_memread, main_3_memtoreg, main_3_memwrite,
       main_3_reg_dst, main_3_regwrite, main_5_zero;
  wire [2:0] main_3_aluop;
  wire [3:0] main_6_out_3;
  wire [4:0] multiplexer_1_out, ram_1_data_2;
  wire [23:0] bitselector_1_out, shifter_1_out;
  wire [31:0] bit_extender_1_out, main_1_alu_result, main_2_rd2, main_4_alu_result, multiplexer_3_out,
       ram_1_data, ram_2_data, shifter_2_out;

  Clock Clock (.out(Clock_out));
  Register #(.width(32)) PC (.D(multiplexer_3_out), .en(1'b1), .Q(out_6), .clk(Clock_out), .clr(in_2));
  BitSelector #(.width(32), .group(24)) bitselector_1 (.in(out_6), .out(bitselector_1_out), .sel(1'b0));
  Shifter #(.width(24), .shift("lr")) shifter_1 (.in(bitselector_1_out), .\dist (in_1), .out(shifter_1_out));
  B23EE1100_Lab9_ALU_main main_1 (
    .INPUT_1(out_6), .INPUT_2(32'h4), .ALU_RESULT(main_1_alu_result), .ALU_Control(4'b0010));  // open: Zero, Carry, Overflow
  RAM #(.addrWidth(24), .dataWidth(32)) ram_1 (
    .addr(shifter_1_out), .data({ram_1_data[31:26], ram_1_data_2, ram_1_data[20:0]}), .ld(1'b1), .clr(in_3));  // open: sel, clk
  B23EE1100_Lab9_registerfile_main main_2 (
    .RD1(out_7), .A1(ram_1_data_2), .WD(out_9), .RD2(main_2_rd2), .RegWrite(main_3_regwrite),
    .A3(multiplexer_1_out), .A2(ram_1_data[20:16]), .Clock(Clock_out), .Reset(Reset));
  Multiplexer #(.width(5), .enable("false")) multiplexer_1 (
    .in0(ram_1_data[20:16]), .in1(ram_1_data[15:11]), .out(multiplexer_1_out), .sel(main_3_reg_dst));
  assign bit_extender_1_out = {{16{ram_1_data[15]}}, ram_1_data[15:0]};  // Bit_Extender bit_extender_1
  B23EE1100_Lab9_MainControlUnit_main main_3 (
    .Opcode(ram_1_data[31:26]), .ALUSrc(main_3_alusrc), .MemToReg(main_3_memtoreg),
    .RegWrite(main_3_regwrite), .MemRead(main_3_memread), .MemWrite(main_3_memwrite), .Branch(main_3_branch),
    .ALUOp(main_3_aluop), .Reg_Dst(main_3_reg_dst));
  B23EE1100_Lab9_ALU_main main_4 (
    .INPUT_1(main_1_alu_result), .INPUT_2(shifter_2_out), .ALU_RESULT(main_4_alu_result),
    .ALU_Control(4'b0010));  // open: Zero, Carry, Overflow
  B23EE1100_Lab9_ALU_main main_5 (
    .INPUT_1(out_7), .INPUT_2(out_8), .Zero(main_5_zero), .ALU_RESULT(out_10), .ALU_Control(main_6_out_3));  // open: Carry, Overflow
  B23EE1100_Lab9_ALUControlUnit_main main_6 (.ALUop(main_3_aluop), .in_2(ram_1_data[5:0]), .out_3(main_6_out_3));
  Shifter #(.width(32)) shifter_2 (.in(bit_extender_1_out), .\dist (5'b00010), .out(shifter_2_out));
  Multiplexer #(.width(32), .enable("false")) multiplexer_2 (
    .in0(main_2_rd2), .in1(bit_extender_1_out), .out(out_8), .sel(main_3_alusrc));
  and and_1 (and_1_out, main_3_branch, main_5_zero);
  BitSelector #(.width(32), .group(24)) bitselector_2 (.in(out_10), .out(out_11), .sel(1'b0));
  Multiplexer #(.width(32), .enable("false")) multiplexer_3 (
    .in0(main_1_alu_result), .in1(main_4_alu_result), .out(multiplexer_3_out), .sel(and_1_out));
  RAM #(.addrWidth(24), .dataWidth(32), .bus("separate")) ram_2 (
    .addr(out_11), .din(main_2_rd2), .data(ram_2_data), .str(main_3_memwrite), .clk(Clock_out),
    .ld(main_3_memread), .clr(Data_Mem_RESET));  // open: sel
  Multiplexer #(.width(32), .enable("false")) multiplexer_4 (
    .in0(out_10), .in1(ram_2_data), .out(out_9), .sel(main_3_memtoreg));

  // Notes on the sheet:
  //   PC'
  //   Bit Selector (32->24)
  //   PC/4
  //   PC
  //   Instruction
  //   Memory
  //   ALUResult
  //   A
  //   B
  //   ALU_RESULT
  //   ALU_OP
  //   Zero
  //   Carry
  //   Overflow
  //   PC+4
  //   Wrtie Data
  //   Wrtie Data
  //   A1
  //   A2
  //   Register 
  //   A3
  //   WD
  //   RD1
  //   RD2
  //   SignExtendIMM
  //   RD2
  //   SignExtendIMM
  //   RD1
  //   ALUSrc
  //   A
  //   B
  //   A
  //   B
  //   Zero
  //   Carry
  //   Overflow
  //   ALU_RESULT
  //   ALU_OP
  //   Zero
  //   Carry
  //   Overflow
  //   ALU_RESULT
  //   Branch
  //   Zerpo
  //   PC+4
  //   PCBranch
  //   PC Src
  //   Bit Selector (32->24)
  //   PC'
  //   MemToReg
  //   MemWrite
  //   MemRead
  //   ALUResult
  //   Mem Write
  //   Mem Read
  //   MemToReg
  //   Wrtie Data
endmodule
