// Logisim project B23EE1100_Lab9_MainControlUnit.circ as structural Verilog: 2 circuits, main circuit main
module main (
  input  [5:0] Opcode,
  output Reg_Dst,
  output ALUSrc,
  output MemToReg,
  output MemRead,
  output MemWrite,
  output Branch,
  output [2:0] ALUOp,
  output RegWrite
);

  wire addi_out_7, andi_out_7, For_R_type_out_7, NOP_out_7, not_1_out, not_2_out, not_3_out, not_4_out,
       not_5_out, not_6_out, not_7_out, not_8_out, not_9_out, not_10_out, not_11_out, not_12_out, not_13_out,
       not_14_out, not_15_out, not_16_out, not_17_out, not_18_out, not_19_out, not_20_out, not_21_out,
       not_22_out, not_23_out, not_24_out, not_25_out, or_2_out, ori_out_7, slti_out_7, subi_out_7;

  not not_1 (not_1_out, Opcode[0]);
  not not_2 (not_2_out, Opcode[3]);
  not not_3 (not_3_out, Opcode[1]);
  not not_4 (not_4_out, Opcode[3]);
  not not_5 (not_5_out, Opcode[2]);
  not not_6 (not_6_out, Opcode[3]);
  not not_7 (not_7_out, Opcode[2]);
  not not_8 (not_8_out, Opcode[0]);
  not not_9 (not_9_out, Opcode[5]);
  not not_10 (not_10_out, Opcode[1]);
  not not_11 (not_11_out, Opcode[0]);
  not not_12 (not_12_out, Opcode[5]);
  not not_13 (not_13_out, Opcode[3]);
  not not_14 (not_14_out, Opcode[5]);
  not not_15 (not_15_out, Opcode[4]);
  not not_16 (not_16_out, Opcode[3]);
  not not_17 (not_17_out, Opcode[2]);
  not not_18 (not_18_out, Opcode[2]);
  not not_19 (not_19_out, Opcode[3]);
  not not_20 (not_20_out, Opcode[3]);
  not not_21 (not_21_out, Opcode[1]);
  not not_22 (not_22_out, Opcode[0]);
  not not_23 (not_23_out, Opcode[1]);
  not not_24 (not_24_out, Opcode[0]);
  InvertAnd For_R_type (
    .in_1(Opcode[5]), .in_2(Opcode[4]), .in_3(Opcode[3]), .in_4(Opcode[2]), .in_5(Opcode[1]),
    .in_6(Opcode[0]), .out_7(For_R_type_out_7));
  InvertAnd For_beq (
    .in_1(Opcode[5]), .in_2(Opcode[4]), .in_3(Opcode[3]), .in_4(not_18_out), .in_5(Opcode[1]),
    .in_6(Opcode[0]), .out_7(Branch));
  InvertAnd addi (
    .in_1(Opcode[5]), .in_2(Opcode[4]), .in_3(not_19_out), .in_4(Opcode[2]), .in_5(Opcode[1]),
    .in_6(Opcode[0]), .out_7(addi_out_7));
  InvertAnd subi (
    .in_1(Opcode[5]), .in_2(Opcode[4]), .in_3(not_20_out), .in_4(Opcode[2]), .in_5(Opcode[1]),
    .in_6(not_1_out), .out_7(subi_out_7));
  InvertAnd slti (
    .in_1(Opcode[5]), .in_2(Opcode[4]), .in_3(not_2_out), .in_4(Opcode[2]), .in_5(not_3_out),
    .in_6(Opcode[0]), .out_7(slti_out_7));
  InvertAnd andi (
    .in_1(Opcode[5]), .in_2(Opcode[4]), .in_3(not_4_out), .in_4(not_5_out), .in_5(Opcode[1]),
    .in_6(Opcode[0]), .out_7(andi_out_7));
  InvertAnd ori (
    .in_1(Opcode[5]), .in_2(Opcode[4]), .in_3(not_6_out), .in_4(not_7_out), .in_5(Opcode[1]),
    .in_6(not_8_out), .out_7(ori_out_7));
  InvertAnd lw (
    .in_1(not_9_out), .in_2(Opcode[4]), .in_3(Opcode[3]), .in_4(Opcode[2]), .in_5(not_10_out),
    .in_6(not_11_out), .out_7(MemRead));
  InvertAnd sw (
    .in_1(not_12_out), .in_2(Opcode[4]), .in_3(not_13_out), .in_4(Opcode[2]), .in_5(not_21_out),
    .in_6(not_22_out), .out_7(MemWrite));
  not not_25 (not_25_out, NOP_out_7);
  InvertAnd NOP (
    .in_1(not_14_out), .in_2(not_15_out), .in_3(not_16_out), .in_4(not_17_out), .in_5(not_23_out),
    .in_6(not_24_out), .out_7(NOP_out_7));
  and and_1 (Reg_Dst, not_25_out, For_R_type_out_7);
  or or_1 (ALUSrc, MemWrite, addi_out_7, subi_out_7, slti_out_7, andi_out_7, ori_out_7, MemRead);
  or or_2 (or_2_out, For_R_type_out_7, addi_out_7, subi_out_7, MemRead, slti_out_7, andi_out_7, ori_out_7);
  and and_2 (RegWrite, not_25_out, or_2_out);
  or or_3 (ALUOp[2], ori_out_7, For_R_type_out_7);
  or or_4 (ALUOp[0], andi_out_7, subi_out_7, For_R_type_out_7);
  or or_5 (ALUOp[1], slti_out_7, andi_out_7);

  assign MemToReg = MemRead;
endmodule

module InvertAnd (
  input  in_1,
  input  in_2,
  input  in_3,
  input  in_4,
  input  in_5,
  input  in_6,
  output out_7
);

  wire not_1_out, not_2_out, not_3_out, not_4_out, not_5_out, not_6_out;

  not not_1 (not_1_out, in_5);
  not not_2 (not_2_out, in_6);
  not not_3 (not_3_out, in_3);
  not not_4 (not_4_out, in_4);
  not not_5 (not_5_out, in_1);
  not not_6 (not_6_out, in_2);
  and and_1 (out_7, not_5_out, not_6_out, not_3_out, not_4_out, not_1_out, not_2_out);
endmodule
